// Logisim project basic.circ as structural Verilog: 19 circuits, main circuit main
module main (
);

  wire button_1_out, switch_1_p1;
  wire [2:0] slider_1_out;

  CLK clk_1 (.in_2(button_1_out), .in_3(switch_1_p1), .in_1(slider_1_out));  // open: out_4
  Slider #(.width(3)) slider_1 (.out(slider_1_out));
  Button button_1 (.out(button_1_out));
  // Switch switch_1: pin names not known; wires that end beside it: switch_1_p1, 1'b1
endmodule

module T_AND (
  input  [1:0] a,
  input  [1:0] b,
  output [1:0] q
);

  or or_1 (q[1], a[1], b[1]);
  and and_1 (q[0], ~a[1], a[0], ~b[1], b[0]);  // AND_Gate
endmodule

module T_OR (
  input  [1:0] a,
  input  [1:0] b,
  output [1:0] q
);

  and and_1 (q[1], a[1], b[1]);
  or or_1 (q[0], a[0], b[0]);
endmodule

module T_NOT (
  input  [1:0] a,
  output [1:0] q
);


  assign q = {a[0], a[1]};
endmodule

module T_HALF_ADDER (
  input  [1:0] a,
  input  [1:0] b,
  output [1:0] q,
  output [1:0] carry
);

  wire and_1_out, and_2_out, and_3_out, and_4_out, and_5_out, and_6_out, not_1_out, not_2_out, not_3_out,
       not_4_out;

  not not_1 (not_1_out, a[1]);
  not not_2 (not_2_out, a[0]);
  not not_3 (not_3_out, b[1]);
  not not_4 (not_4_out, b[0]);
  and and_1 (and_1_out, not_1_out, not_2_out, b[1]);
  and and_2 (and_2_out, a[0], b[0]);
  and and_3 (and_3_out, a[1], not_3_out, not_4_out);
  and and_4 (and_4_out, not_1_out, not_2_out, b[0]);
  and and_5 (and_5_out, a[0], not_3_out, not_4_out);
  and and_6 (and_6_out, a[1], b[1]);
  and and_7 (carry[1], a[1], b[1]);
  and and_8 (carry[0], a[0], b[0]);
  or or_1 (q[1], and_1_out, and_2_out, and_3_out);
  or or_2 (q[0], and_4_out, and_5_out, and_6_out);
endmodule

module T_FULL_ADDER (
  input  [1:0] A,
  input  [1:0] CARRY_IN,
  input  [1:0] B,
  output [1:0] CARRY_OUT,
  output [1:0] SUM
);

  wire [1:0] conv_1_x, conv_2_x, conv_3_x, t_half_adder_2_carry, t_half_adder_3_carry, t_half_adder_3_q;

  T_HALF_ADDER t_half_adder_1 (.a(t_half_adder_2_carry), .b(t_half_adder_3_carry), .q(CARRY_OUT));  // open: carry
  T_HALF_ADDER t_half_adder_2 (.a(CARRY_IN), .b(t_half_adder_3_q), .q(SUM), .carry(t_half_adder_2_carry));
  // Probe on conv_1_x
  conv conv_1 (.a(A), .x(conv_1_x));
  T_HALF_ADDER t_half_adder_3 (.a(B), .b(A), .q(t_half_adder_3_q), .carry(t_half_adder_3_carry));
  // Probe on conv_2_x
  conv conv_2 (.a(CARRY_IN), .x(conv_2_x));
  // Probe on conv_3_x
  conv conv_3 (.a(B), .x(conv_3_x));
endmodule

module conv (
  input  [1:0] a,
  output [1:0] x
);

  wire and_1_out, and_2_out, not_1_out, not_2_out;

  not not_1 (not_1_out, a[1]);
  not not_2 (not_2_out, a[0]);
  and and_1 (and_1_out, not_1_out, a[0]);
  and and_2 (and_2_out, a[1], not_2_out);
  or or_1 (x[0], and_1_out, and_2_out);

  assign x[1] = a[1];
endmodule

module TRYTE_ADDER (
  input  [9:0] A,
  input  [1:0] CIN,
  input  [9:0] B,
  output [1:0] COUT,
  output [9:0] SUM
);

  wire [1:0] t_full_adder_2_carry_out, t_full_adder_3_carry_out, t_full_adder_4_carry_out,
       t_full_adder_5_carry_out;

  T_FULL_ADDER t_full_adder_1 (
    .CARRY_OUT(COUT), .SUM(SUM[9:8]), .A(A[9:8]), .B(B[9:8]), .CARRY_IN(t_full_adder_2_carry_out));
  T_FULL_ADDER t_full_adder_2 (
    .CARRY_OUT(t_full_adder_2_carry_out), .SUM(SUM[7:6]), .A(A[7:6]), .B(B[7:6]),
    .CARRY_IN(t_full_adder_3_carry_out));
  T_FULL_ADDER t_full_adder_3 (
    .CARRY_OUT(t_full_adder_3_carry_out), .SUM(SUM[5:4]), .A(A[5:4]), .B(B[5:4]),
    .CARRY_IN(t_full_adder_4_carry_out));
  T_FULL_ADDER t_full_adder_4 (
    .CARRY_OUT(t_full_adder_4_carry_out), .SUM(SUM[3:2]), .A(A[3:2]), .B(B[3:2]),
    .CARRY_IN(t_full_adder_5_carry_out));
  T_FULL_ADDER t_full_adder_5 (
    .CARRY_OUT(t_full_adder_5_carry_out), .SUM(SUM[1:0]), .A(A[1:0]), .B(B[1:0]), .CARRY_IN(CIN));
endmodule

module TRYTE_NOT (
  input  [9:0] in_1,
  output [9:0] out_2
);

  T_NOT t_not_1 (.a(in_1[9:8]), .q(out_2[9:8]));
  T_NOT t_not_2 (.a(in_1[7:6]), .q(out_2[7:6]));
  T_NOT t_not_3 (.a(in_1[5:4]), .q(out_2[5:4]));
  T_NOT t_not_4 (.a(in_1[3:2]), .q(out_2[3:2]));
  T_NOT t_not_5 (.a(in_1[1:0]), .q(out_2[1:0]));
endmodule

module T_MUX_2X1 (
  input  [1:0] in_1,
  input  [1:0] in_2,
  input  in_3,
  output [1:0] out_4
);

  wire [1:0] bit_extender_1_out, subtractor_1_out, t_and_1_q, t_and_2_q, t_not_1_q;

  assign bit_extender_1_out = {{1{in_3}}, in_3};  // Bit_Extender bit_extender_1
  T_NOT t_not_1 (.a(subtractor_1_out), .q(t_not_1_q));
  // Probe on subtractor_1_out
  Subtractor #(.width(2)) subtractor_1 (.a(bit_extender_1_out), .b(2'b10), .out(subtractor_1_out));  // open: bin, bout
  T_AND t_and_1 (.a(in_1), .b(t_not_1_q), .q(t_and_1_q));
  T_AND t_and_2 (.a(in_2), .b(subtractor_1_out), .q(t_and_2_q));
  T_OR t_or_1 (.a(t_and_1_q), .b(t_and_2_q), .q(out_4));
endmodule

module T_NAND (
  input  [1:0] in_1,
  input  [1:0] in_2,
  output [1:0] out_3
);

  wire [1:0] t_and_1_q;

  T_AND t_and_1 (.a(in_1), .b(in_2), .q(t_and_1_q));
  T_NOT t_not_1 (.a(t_and_1_q), .q(out_3));
endmodule

module T_FLIP_FLOP (
  input  in_1,
  input  [1:0] in_2,
  output [1:0] out_3
);

  D_Flip_Flop d_ff_1 (.clk(in_1), .D(in_2[1]), .Q(out_3[1]));  // open: Qn, preset, reset
  D_Flip_Flop d_ff_2 (.clk(in_1), .D(in_2[0]), .Q(out_3[0]));  // open: Qn, preset, reset
endmodule

module TRYTE_REGISTER (
  input  in_1,
  input  [9:0] in_2,
  output [9:0] out_3
);

  T_FLIP_FLOP t_flip_flop_1 (.in_1(in_1), .in_2(in_2[9:8]), .out_3(out_3[9:8]));
  T_FLIP_FLOP t_flip_flop_2 (.in_1(in_1), .in_2(in_2[7:6]), .out_3(out_3[7:6]));
  T_FLIP_FLOP t_flip_flop_3 (.in_1(in_1), .in_2(in_2[5:4]), .out_3(out_3[5:4]));
  T_FLIP_FLOP t_flip_flop_4 (.in_1(in_1), .in_2(in_2[3:2]), .out_3(out_3[3:2]));
  T_FLIP_FLOP t_flip_flop_5 (.in_1(in_1), .in_2(in_2[1:0]), .out_3(out_3[1:0]));
endmodule

module CLK (
  input  [2:0] in_1,
  input  in_2,
  input  in_3,
  output out_4
);

  wire clock_1_out, multiplexer_1_out, not_1_out, not_2_out, not_3_out, not_4_out, not_5_out, t_ff_1_q,
       t_ff_2_q, t_ff_3_q, t_ff_4_q, t_ff_5_q, t_ff_6_q, t_ff_7_q, undriven;

  Clock clock_1 (.out(clock_1_out));
  T_Flip_Flop t_ff_1 (.clk(clock_1_out), .T(clock_1_out), .Q(t_ff_1_q));  // open: Qn, preset, reset
  T_Flip_Flop t_ff_2 (.clk(t_ff_1_q), .T(t_ff_1_q), .Q(t_ff_2_q));  // open: Qn, preset, reset
  T_Flip_Flop t_ff_3 (.clk(t_ff_2_q), .T(t_ff_2_q), .Q(t_ff_3_q));  // open: Qn, preset, reset
  T_Flip_Flop t_ff_4 (.clk(t_ff_3_q), .T(t_ff_3_q), .Q(t_ff_4_q));  // open: Qn, preset, reset
  Multiplexer #(.select(3)) multiplexer_1 (
    .in0(clock_1_out), .in1(t_ff_1_q), .in2(t_ff_2_q), .in3(t_ff_3_q), .in4(t_ff_4_q), .in5(t_ff_5_q),
    .in6(t_ff_6_q), .in7(t_ff_7_q), .out(multiplexer_1_out), .sel(in_1));
  T_Flip_Flop t_ff_5 (.clk(t_ff_4_q), .T(t_ff_4_q), .Q(t_ff_5_q));  // open: Qn, preset, reset
  Multiplexer multiplexer_2 (.in0(multiplexer_1_out), .in1(in_2), .out(out_4), .sel(in_3));
  T_Flip_Flop t_ff_6 (.clk(t_ff_5_q), .T(t_ff_5_q), .Q(t_ff_6_q));  // open: Qn, preset, reset
  not not_1 (not_1_out, undriven);
  not not_2 (not_2_out, not_1_out);
  not not_3 (not_3_out, not_2_out);
  T_Flip_Flop t_ff_7 (.clk(t_ff_6_q), .T(t_ff_6_q), .Q(t_ff_7_q));  // open: Qn, preset, reset
  not not_4 (not_4_out, not_3_out);
  not not_5 (not_5_out, not_4_out);
  // AND_Gate and_1 has open pins: in0=not_5_out, in1=undriven, out=open
endmodule

module TRYTE_SUBTRAcTOR (
  input  [9:0] in_1,
  input  [1:0] in_2,
  input  [9:0] in_3,
  output [1:0] out_4,
  output [9:0] out_5
);

  wire [9:0] tryte_not_1_out_2;

  TRYTE_ADDER tryte_adder_1 (.A(in_1), .B(tryte_not_1_out_2), .CIN(in_2), .SUM(out_5), .COUT(out_4));
  TRYTE_NOT tryte_not_1 (.in_1(in_3), .out_2(tryte_not_1_out_2));
endmodule

module ULA (
  input  [11:0] in_1,
  input  [11:0] in_2,
  input  [11:0] in_3
);
endmodule

module TRYTE_SHIFT_LEFT (
  input  [9:0] in_1,
  output [9:0] out_2
);


  assign out_2 = {in_1[7:0], 2'b00};
endmodule

module TRYTE_SHIFT_RIGHT (
  input  [9:0] in_1,
  output [9:0] out_2
);


  assign out_2 = {2'b00, in_1[9:2]};
endmodule

module TRYTE_DISPLAY (
  input  [9:0] in_1,
  output out_2,
  output out_3,
  output out_4,
  output out_5,
  output out_6
);

  Multiplexer #(.select(2)) multiplexer_1 (.in0(1'b0), .in1(1'b1), .out(out_2), .sel(in_1[9:8]));  // open: in2, in3
  Multiplexer #(.select(2)) multiplexer_2 (.in0(1'b0), .in1(1'b1), .out(out_3), .sel(in_1[7:6]));  // open: in2, in3
  Multiplexer #(.select(2)) multiplexer_3 (.in0(1'b0), .in1(1'b1), .out(out_4), .sel(in_1[5:4]));  // open: in2, in3
  Multiplexer #(.select(2)) multiplexer_4 (.in0(1'b0), .in1(1'b1), .out(out_5), .sel(in_1[3:2]));  // open: in2, in3
  Multiplexer #(.select(2)) multiplexer_5 (.in0(1'b0), .in1(1'b1), .out(out_6), .sel(in_1[1:0]));  // open: in2, in3
endmodule
