// Logisim project basic_T.circ as structural Verilog
module T_NOT (
  input  [1:0] a,
  output [1:0] q
);


  assign q = {a[0], a[1]};
endmodule

module T_OR (
  input  [1:0] a,
  input  [1:0] b,
  output [1:0] q
);

  and and_1 (q[1], a[1], b[1]);
  or or_1 (q[0], a[0], b[0]);
endmodule

module T_AND (
  input  [1:0] a,
  input  [1:0] b,
  output [1:0] q
);

  or or_1 (q[1], a[1], b[1]);
  and and_1 (q[0], ~a[1], a[0], ~b[1], b[0]);  // AND_Gate
endmodule

module T_NOR (
  input  [1:0] A,
  input  [1:0] B,
  output [1:0] out_3
);

  wire [1:0] t_or_1_q;

  T_OR t_or_1 (.a(A), .b(B), .q(t_or_1_q));
  T_NOT t_not_1 (.a(t_or_1_q), .q(out_3));
endmodule

module T_NAND (
  input  [1:0] in_1,
  input  [1:0] in_2,
  output [1:0] out_3
);

  wire [1:0] t_and_1_q;

  T_AND t_and_1 (.a(in_1), .b(in_2), .q(t_and_1_q));
  T_NOT t_not_1 (.a(t_and_1_q), .q(out_3));
endmodule

module T_XOR (
  input  [1:0] A,
  input  [1:0] B,
  output [1:0] out_3
);

  T_HALF_ADDER t_half_adder_1 (.A(A), .B(B), .SUM(out_3));  // open: CARRY_OUT
endmodule

module T_HALF_ADDER (
  input  [1:0] A,
  input  [1:0] B,
  output [1:0] SUM,
  output [1:0] CARRY_OUT
);

  wire and_1_out, and_2_out, and_3_out, and_4_out, and_5_out, and_6_out, not_1_out, not_2_out, not_3_out,
       not_4_out;

  not not_1 (not_1_out, A[1]);
  not not_2 (not_2_out, A[0]);
  not not_3 (not_3_out, B[1]);
  not not_4 (not_4_out, B[0]);
  and and_1 (and_1_out, not_1_out, not_2_out, B[1]);
  and and_2 (and_2_out, A[0], B[0]);
  and and_3 (and_3_out, A[1], not_3_out, not_4_out);
  and and_4 (and_4_out, not_1_out, not_2_out, B[0]);
  and and_5 (and_5_out, A[0], not_3_out, not_4_out);
  and and_6 (and_6_out, A[1], B[1]);
  and and_7 (CARRY_OUT[1], A[1], B[1]);
  and and_8 (CARRY_OUT[0], A[0], B[0]);
  or or_1 (SUM[1], and_1_out, and_2_out, and_3_out);
  or or_2 (SUM[0], and_4_out, and_5_out, and_6_out);
endmodule

module T_FULL_ADDER (
  input  [1:0] A,
  input  [1:0] CARRY_IN,
  input  [1:0] B,
  output [1:0] CARRY_OUT,
  output [1:0] SUM
);

  wire [1:0] t_half_adder_2_carry_out, t_half_adder_3_carry_out, t_half_adder_3_sum;

  T_HALF_ADDER t_half_adder_1 (
    .A(t_half_adder_2_carry_out), .B(t_half_adder_3_carry_out), .SUM(CARRY_OUT));  // open: CARRY_OUT
  T_HALF_ADDER t_half_adder_2 (.A(CARRY_IN), .B(t_half_adder_3_sum), .SUM(SUM), .CARRY_OUT(t_half_adder_2_carry_out));
  T_HALF_ADDER t_half_adder_3 (.A(B), .B(A), .SUM(t_half_adder_3_sum), .CARRY_OUT(t_half_adder_3_carry_out));
endmodule

module T_FLIP_FLOP (
  input  in_1,
  input  [1:0] in_2,
  output [1:0] out_3
);

  D_Flip_Flop d_ff_1 (.clk(in_1), .D(in_2[1]), .Q(out_3[1]));  // open: Qn, preset, reset
  D_Flip_Flop d_ff_2 (.clk(in_1), .D(in_2[0]), .Q(out_3[0]));  // open: Qn, preset, reset
endmodule

module T_MUX_2X1 (
  input  [1:0] in_1,
  input  [1:0] in_2,
  input  in_3,
  output [1:0] out_4
);

  wire [1:0] bit_extender_1_out, subtractor_1_out, t_and_1_q, t_and_2_q, t_not_1_q;

  assign bit_extender_1_out = {{1{in_3}}, in_3};  // Bit_Extender bit_extender_1
  T_NOT t_not_1 (.a(subtractor_1_out), .q(t_not_1_q));
  // Probe on subtractor_1_out
  Subtractor #(.width(2)) subtractor_1 (.a(bit_extender_1_out), .b(2'b10), .out(subtractor_1_out));  // open: bin, bout
  T_AND t_and_1 (.a(in_1), .b(t_not_1_q), .q(t_and_1_q));
  T_AND t_and_2 (.a(in_2), .b(subtractor_1_out), .q(t_and_2_q));
  T_OR t_or_1 (.a(t_and_1_q), .b(t_and_2_q), .q(out_4));
endmodule
